# Fritzing sketch 1.1.1_BlinkingLed (saved by Fritzing 0.9.3b)
breadboards: 1

parts:
  LED1 = LED - 5mm [color="Red (633nm)" package="5 mm [THT]"]
  R1 = Resistor [tolerance=±5% resistance=220 package=THT]
  T-Cobbler1 = GPIO Extension Board

nets:
  N1: LED1.cathode, T-Cobbler1.#17
  N2: LED1.anode, R1.Pin_1
  N3: R1.Pin_0, T-Cobbler1.3V3

custom parts:
  GPIO Extension Board: T-Cobbler for RPi B+ and Rpi2 from SunFounder
