# Fritzing sketch 1.1.3_LedBarGraph (saved by Fritzing 0.9.3b)
breadboards: 1

parts:
  T-Cobbler1 = GPIO Extension Board
  R1 = Resistor [tolerance=±5% resistance=220 package=THT]
  D1 = LED_BARGRAPH_10 [package=led_bargaph_10]
  R2 = Resistor [tolerance=±5% resistance=220 package=THT]
  R3 = Resistor [tolerance=±5% resistance=220 package=THT]
  R4 = Resistor [tolerance=±5% resistance=220 package=THT]
  R5 = Resistor [tolerance=±5% resistance=220 package=THT]
  R6 = Resistor [tolerance=±5% resistance=220 package=THT]
  R7 = Resistor [tolerance=±5% resistance=220 package=THT]
  R8 = Resistor [tolerance=±5% resistance=220 package=THT]
  R9 = Resistor [tolerance=±5% resistance=220 package=THT]
  R10 = Resistor [tolerance=±5% resistance=220 package=THT]

nets:
  N1: T-Cobbler1.3V3, R1.Pin_0, R2.Pin_0, R3.Pin_0, R4.Pin_0, R5.Pin_0, R6.Pin_0, R7.Pin_0, R8.Pin_0, R9.Pin_0, R10.Pin_0
  N2: T-Cobbler1.SDA1, D1.H_C
  N3: T-Cobbler1.SCL1, D1.I_C
  N4: T-Cobbler1.#17, D1.A_C
  N5: T-Cobbler1.#27, D1.C_C
  N6: T-Cobbler1.#22, D1.D_C
  N7: T-Cobbler1.#18, D1.B_C
  N8: T-Cobbler1.#23, D1.E_C
  N9: T-Cobbler1.#24, D1.F_C
  N10: T-Cobbler1.#25, D1.G_C
  N11: T-Cobbler1.CE0, D1.J_C
  N12: R1.Pin_1, D1.A_A
  N13: D1.B_A, R2.Pin_1
  N14: D1.C_A, R3.Pin_1
  N15: D1.D_A, R4.Pin_1
  N16: D1.E_A, R5.Pin_1
  N17: D1.F_A, R6.Pin_1
  N18: D1.G_A, R7.Pin_1
  N19: D1.H_A, R8.Pin_1
  N20: D1.I_A, R9.Pin_1
  N21: D1.J_A, R10.Pin_1

custom parts:
  GPIO Extension Board: T-Cobbler for RPi B+ and Rpi2 from SunFounder
