# Fritzing sketch 1.1.4_7-Segment (saved by Fritzing 0.9.3b)
breadboards: 1

parts:
  T-Cobbler1 = T-Cobbler
  R1 = Resistor [tolerance=±5% resistance=220 package=THT]
  U1 = 74HC595 [package="DIP16 [THT]"]
  DI1 = 7-Segment LED Display [package=THT]

nets:
  3V3: T-Cobbler1.3V3, U1.MR, U1.VCC
  N1: T-Cobbler1.GND#4, R1.Pin_0, U1.GND
  N2: T-Cobbler1.#17, U1.DS
  N3: T-Cobbler1.#27, U1.SH_CP
  N4: T-Cobbler1.GND#22, U1.OE
  N5: T-Cobbler1.#18, U1.ST_CP
  N6: R1.Pin_1, DI1.commAnode#2
  N7: U1.Q1, DI1.cathodeB
  N8: U1.Q2, DI1.cathodeC
  N9: U1.Q3, DI1.cathodeD
  N10: U1.Q4, DI1.cathodeE
  N11: U1.Q5, DI1.cathodeF
  N12: U1.Q6, DI1.cathodeG
  N13: U1.Q7, DI1.cathodeDP
  N14: U1.Q0, DI1.cathodeA

custom parts:
  T-Cobbler: T-Cobbler for RPi B+ and Rpi2 from SunFounder
