# Fritzing sketch 1.1.5_4-Digit (saved by Fritzing 0.9.3b)
breadboards: 1

parts:
  T-Cobbler1 = T-Cobbler
  R1 = Resistor [tolerance=±5% resistance=1k package=THT]
  U1 = 74HC595 [package="DIP16 [THT]"]
  Q1 = PNP-Transistor [package="TO92 [THT]"]
  Q2 = PNP-Transistor [package="TO92 [THT]"]
  Q3 = PNP-Transistor [package="TO92 [THT]"]
  Q4 = PNP-Transistor [package="TO92 [THT]"]
  LED1 = 7-SEGMENT-4DIGIT-YOUNGSUN [package=7-segment-4digit-youngsun-longpads]
  R3 = Resistor [tolerance=±5% resistance=1k package=THT]
  R4 = Resistor [tolerance=±5% resistance=1k package=THT]
  R5 = Resistor [tolerance=±5% resistance=1k package=THT]
  R6 = Resistor [tolerance=±5% resistance=220 package=THT]
  R7 = Resistor [tolerance=±5% resistance=220 package=THT]
  R8 = Resistor [tolerance=±5% resistance=220 package=THT]
  R9 = Resistor [tolerance=±5% resistance=220 package=THT]
  R10 = Resistor [tolerance=±5% resistance=220 package=THT]
  R11 = Resistor [tolerance=±5% resistance=220 package=THT]
  R12 = Resistor [tolerance=±5% resistance=220 package=THT]
  R13 = Resistor [tolerance=±5% resistance=220 package=THT]

nets:
  3V3: T-Cobbler1.3V3, U1.MR, U1.VCC, Q1.E, Q2.E, Q3.E, Q4.E
  N1: T-Cobbler1.GND#4, U1.GND
  N2: T-Cobbler1.#17, R5.Pin_0
  N3: T-Cobbler1.#27, R4.Pin_0
  N4: T-Cobbler1.#22, R3.Pin_0
  N5: T-Cobbler1.MOSI, R1.Pin_0
  N6: T-Cobbler1.GND#22, U1.OE
  N7: T-Cobbler1.#18, U1.SH_CP
  N8: T-Cobbler1.#23, U1.ST_CP
  N9: T-Cobbler1.#24, U1.DS
  N10: R1.Pin_1, Q1.B
  N11: U1.Q1, R7.Pin_1
  N12: U1.Q2, R8.Pin_1
  N13: U1.Q3, R9.Pin_0
  N14: U1.Q4, R10.Pin_0
  N15: U1.Q5, R11.Pin_0
  N16: U1.Q6, R12.Pin_1
  N17: U1.Q7, R13.Pin_0
  N18: U1.Q0, R6.Pin_0
  N19: Q1.C, LED1.DP
  N20: Q2.B, R3.Pin_1
  N21: Q2.C, LED1.F
  N22: Q3.B, R4.Pin_1
  N23: Q3.C, LED1.COL-C
  N24: Q4.B, R5.Pin_1
  N25: Q4.C, LED1.G
  N26: LED1.DIG2, R10.Pin_1
  N27: LED1.D, R9.Pin_1
  N28: LED1.COL-A, R13.Pin_1
  N29: LED1.E, R8.Pin_0
  N30: LED1.DIG3, R12.Pin_0
  N31: LED1.APOS-A, R7.Pin_0
  N32: LED1.C, R11.Pin_1
  N33: LED1.A, R6.Pin_1

custom parts:
  T-Cobbler: T-Cobbler for RPi B+ and Rpi2 from SunFounder
  7-SEGMENT-4DIGIT-YOUNGSUN: This is a part for the 4-Digit 7-segment LEDs from Young Sun. Different from the Digikey LEDs, all 16 pins are used. The LONGPADS Variant is used for a test jig, but you may like it because there is more pad to solder to. If you are concerned about routing space, the standard works just fine though.
