# Fritzing sketch 1.1.6_LedMatrix (saved by Fritzing 0.9.3b)
breadboards: 1

parts:
  T-Cobbler1 = T-Cobbler
  U1 = 74HC595 [package="DIP16 [THT]"]
  U2 = 74HC595 [package="DIP16 [THT]"]
  module2 = 788BS Dot matix

nets:
  VCC: T-Cobbler1.3V3, U1.MR, U1.VCC, U2.MR, U2.VCC
  GND: T-Cobbler1.GND#4, U1.GND, U2.GND
  N1: T-Cobbler1.#17, U2.DS
  N2: T-Cobbler1.#27, U1.SH_CP, U2.SH_CP
  N3: T-Cobbler1.GND#22, U1.OE, U2.OE
  N4: T-Cobbler1.#18, U1.ST_CP, U2.ST_CP
  N5: U1.Q1, module2.P6
  N6: U1.Q2, module2.P5
  N7: U1.Q3, module2.P10
  N8: U1.Q4, module2.P3
  N9: U1.Q5, module2.P11
  N10: U1.Q6, module2.P15
  N11: U1.Q7, module2.P16
  N12: U1.DS, U2.Q7'
  N13: U1.Q0, module2.P13
  N14: U2.Q1, module2.P14
  N15: U2.Q2, module2.P1
  N16: U2.Q3, module2.P12
  N17: U2.Q4, module2.P8
  N18: U2.Q5, module2.P2
  N19: U2.Q6, module2.P7
  N20: U2.Q7, module2.P4
  N21: U2.Q0, module2.P9

custom parts:
  T-Cobbler: T-Cobbler for RPi B+ and Rpi2 from SunFounder
  788BS Dot matix: 788BS 8x8 dot matix from SunFounder
