# Fritzing sketch 1.1.7_I2C Lcd1602 (saved by Fritzing 0.9.3b)
breadboards: 1

parts:
  T-Cobbler1 = T-Cobbler
  module1 = I2C LCD1602

nets:
  N1: T-Cobbler1.SDA, module1.SDA
  N2: T-Cobbler1.SCL, module1.SCL
  N3: T-Cobbler1.5.0V#20, module1.VCC
  N4: T-Cobbler1.GND#22, module1.GND

custom parts:
  T-Cobbler: T-Cobbler for RPi B+ and Rpi2 from SunFounder
  I2C LCD1602: I2C LCD1602 module of SunFounder Sensor Kit
