# Fritzing sketch 1.2.2_PassiveBuzzer (saved by Fritzing 0.9.3b)
breadboards: 1

parts:
  T-Cobbler1 = T-Cobbler
  S1 = buzzer [package="[THT]"]
  R1 = Resistor [tolerance=±10% resistance=1k package=THT]
  Q1 = PNP-Transistor [package="TO92 [THT]"]

nets:
  3V3: T-Cobbler1.3V3, S1.VCC
  N1: T-Cobbler1.GND#4, Q1.C
  N2: T-Cobbler1.#17, R1.Pin_1
  N3: S1.GND, Q1.E
  N4: R1.Pin_0, Q1.B

custom parts:
  T-Cobbler: T-Cobbler for RPi B+ and Rpi2 from SunFounder
