# Fritzing sketch 1.3.1_Motor (saved by Fritzing 0.9.3b)
breadboards: 1

parts:
  T-Cobbler1 = GPIO Extension Board
  IC1 = L293D [package=THT]
  IC2 = Power Module V1.0 [package=THT]
  M1 = DC Motor

nets:
  N1: T-Cobbler1.GND#4, IC1.0V, IC2.-#4
  N2: T-Cobbler1.#27, IC1.In_1
  N3: T-Cobbler1.#22, IC1.Enable_1
  N4: IC1.Out_1_(_Controlled_by_Enable_1_), M1.pin_1
  N5: IC1.Out_2_(_Controlled_by_Enable_1_), M1.pin_2
  N6: IC1.+Vmotor, IC2.+#2
  N7: IC1.+V, IC2.+#3

custom parts:
  GPIO Extension Board: T-Cobbler for RPi B+ and Rpi2 from SunFounder
  Power Module V1.0: Power Module used for BreadBoard www.sunfounder.com
