# Fritzing sketch 1.3.2_Servo (saved by Fritzing 0.9.3b)
breadboards: 1

parts:
  T-Cobbler1 = T-Cobbler
  module1 = Servo

nets:
  N1: T-Cobbler1.3V3, module1.Red
  N2: T-Cobbler1.#18, module1.Orange
  N3: T-Cobbler1.GND#36, module1.Brown

custom parts:
  T-Cobbler: T-Cobbler for RPi B+ and Rpi2 from SunFounder
  Servo: servo
