# Fritzing sketch 1.3.3_SteppingMotor (saved by Fritzing 0.9.3b)
breadboards: 1

parts:
  T-Cobbler1 = T-Cobbler
  IC2 = Power Module V1.0 [package=THT]
  U1 = Stepper Motor Driver-v1.0 [package="DIP28 [THT]"]
  module1 = Step Motor

nets:
  N1: T-Cobbler1.GND#22, IC2.-#5, U1.-
  N2: T-Cobbler1.#18, U1.IN1
  N3: T-Cobbler1.#23, U1.IN2
  N4: T-Cobbler1.#24, U1.IN3
  N5: T-Cobbler1.#25, U1.IN4
  N6: IC2.3.3V, IC2.-#4
  N7: IC2.+#2, IC2.GND
  N8: IC2.+#3, U1.+
  N9: U1.OUT1, module1.blue
  N10: U1.OUT2, module1.pink
  N11: U1.OUT3, module1.yellow
  N12: U1.OUT4, module1.orange
  N13: U1.COM, module1.red

custom parts:
  T-Cobbler: T-Cobbler for RPi B+ and Rpi2 from SunFounder
  Power Module V1.0: Power Module used for BreadBoard www.sunfounder.com
  Stepper Motor Driver-v1.0: Stepper Motor Driver
  Step Motor: step motor
