# Fritzing sketch 1.3.4_relay (saved by Fritzing 0.9.3b)
breadboards: 1

parts:
  T-Cobbler1 = GPIO Extension Board
  K1 = Relay [part_number=FRS1B-S package=THT]
  Q1 = NPN-Transistor [package="TO92 [THT]"]
  D1 = Zener Diode [part_number=1N4732A breakdown_voltage=3.6V package="Melf DO-213 AB [SMD]"]
  R1 = Resistor [tolerance=±5% resistance=220 package=THT]
  LED1 = LED - 5mm [color="Red (633nm)" package="5 mm [THT]"]
  R2 = Resistor [tolerance=±5% resistance=1k package=THT]

nets:
  N1: T-Cobbler1.GND#4, Q1.E, LED1.cathode
  N2: T-Cobbler1.#17, R2.Pin_1
  N3: T-Cobbler1.5.0V#20, K1.C1, K1.C2, K1.COIL2, D1.cathode
  N4: K1.COIL1, Q1.C, D1.anode
  N5: K1.B, R1.Pin_0
  N6: Q1.B, R2.Pin_0
  N7: R1.Pin_1, LED1.anode

custom parts:
  GPIO Extension Board: T-Cobbler for RPi B+ and Rpi2 from SunFounder
  Relay: An SPDT relay.
