# Fritzing sketch 2.1.2_Slider (saved by Fritzing 0.9.3b)
breadboards: 1

parts:
  T-Cobbler1 = GPIO Extension Board
  LED1 = LED - 5mm [color="Red (633nm)" package="5 mm [THT]"]
  R1 = Resistor [tolerance=±5% resistance=220 package=THT]
  LED2 = LED - 5mm [color="Yellow (592nm)" package="5 mm [THT]"]
  R2 = Resistor [tolerance=±5% resistance=220 package=THT]
  S1 = Toggle Switch [package=THT]
  R3 = Resistor [tolerance=±5% resistance=10k package=THT]
  C2 = Capacitor [package=cap-pth-small2]

nets:
  N1: T-Cobbler1.3V3, R1.Pin_1, R2.Pin_1, S1.L2
  N2: T-Cobbler1.GND#4, S1.L1, R3.Pin_0, C2.1
  N3: T-Cobbler1.#17, S1.COM, R3.Pin_1, C2.2
  N4: T-Cobbler1.#27, LED2.cathode
  N5: T-Cobbler1.#22, LED1.cathode
  N6: LED1.anode, R2.Pin_0
  N7: R1.Pin_0, LED2.anode

custom parts:
  GPIO Extension Board: T-Cobbler for RPi B+ and Rpi2 from SunFounder
  Capacitor: Capacitor Standard 0603 ceramic capacitor, and 0.1 leaded capacitor.
