# Fritzing sketch 2.1.3_Tilt Switch (saved by Fritzing 0.9.3b)
breadboards: 1

parts:
  T-Cobbler1 = GPIO Extension Board
  LED1 = LED - 5mm [color="Red (633nm)" package="5 mm [THT]"]
  LED2 = LED - 5mm [color="Yellow (595nm)" package="5 mm [THT]"]
  R2 = Resistor [tolerance=±5% resistance=220 package=THT]
  R3 = Resistor [tolerance=±5% resistance=220 package=THT]
  IC1 = Tilt Switch [package="[THT]"]
  R4 = Resistor [tolerance=±5% resistance=10k package=THT]

nets:
  N1: T-Cobbler1.#17, IC1.pin1, R4.Pin_0
  N2: T-Cobbler1.#27, LED2.anode
  N3: T-Cobbler1.#22, LED1.anode
  N4: T-Cobbler1.3.3V, R4.Pin_1
  N5: T-Cobbler1.GND#12, R2.Pin_1, R3.Pin_1, IC1.pin2
  N6: LED1.cathode, R3.Pin_0
  N7: LED2.cathode, R2.Pin_0

custom parts:
  GPIO Extension Board: T-Cobbler for RPi B+ and Rpi2 from SunFounder
  Tilt Switch: This is a ball tilt-switch with a metal ball inside. It is used to detect inclinations of a small angle.
