# Fritzing sketch 2.1.3_relay (saved by Fritzing 0.9.3b)
breadboards: 1

parts:
  T-Cobbler1 = T-Cobbler
  K1 = Relay [part_number=FRS1B-S package=THT]
  Q1 = NPN-Transistor [package="TO92 [THT]"]
  D1 = Zener Diode [part_number=1N4732A breakdown_voltage=3.6V package="Melf DO-213 AB [SMD]"]
  R1 = Resistor [tolerance=±5% resistance=220 package=THT]
  LED1 = LED - 5mm [color="Red (633nm)" package="5 mm [THT]"]

nets:
  N1: T-Cobbler1.GND#4, Q1.E, LED1.cathode
  N2: T-Cobbler1.#17, Q1.B
  N3: T-Cobbler1.5.0V#20, K1.C1, K1.C2, K1.COIL2, D1.cathode
  N4: K1.COIL1, Q1.C, D1.anode
  N5: K1.B, R1.Pin_0
  N6: R1.Pin_1, LED1.anode

custom parts:
  T-Cobbler: T-Cobbler for RPi B+ and Rpi2 from SunFounder
  Relay: An SPDT relay.
