# Fritzing sketch 2.1.4_Potentiometer (saved by Fritzing 0.9.3b)
breadboards: 1

parts:
  T-Cobbler1 = GPIO Extension Board
  R1 = Potentiometer [package=THT]
  IC1 = IC, DIP package, 14 pins [chip_label=ADC0834]
  R2 = Resistor [tolerance=±5% resistance=220 package=THT]
  LED1 = LED - 5mm [color="Red (633nm)" package="5 mm [THT]"]

nets:
  N1: T-Cobbler1.#17, IC1.pin2
  N2: T-Cobbler1.#27, IC1.pin10, IC1.pin13
  N3: T-Cobbler1.#22, R2.Pin_1
  N4: T-Cobbler1.5.0V#20, R1.leg2, IC1.pin1, IC1.pin9, IC1.pin14
  N5: T-Cobbler1.GND#22, R1.leg1, IC1.pin7, IC1.pin8, LED1.cathode
  N6: T-Cobbler1.#18, IC1.pin12
  N7: R1.wiper, IC1.pin3
  N8: R2.Pin_0, LED1.anode

custom parts:
  GPIO Extension Board: T-Cobbler for RPi B+ and Rpi2 from SunFounder
  Potentiometer: A standard adjustable resistor (potentiometer).
