# Fritzing sketch 2.1.6_Joystick (saved by Fritzing 0.9.3b)
breadboards: 1

parts:
  T-Cobbler1 = GPIO Extension Board
  IC1 = IC, DIP package, 14 pins [chip_label=ADC0834]
  S1 = Joystick PS2 v1.0 [package=THT]
  R1 = Resistor [tolerance=±5% resistance=10k package=THT]

nets:
  N1: T-Cobbler1.#17, IC1.pin2
  N2: T-Cobbler1.#27, IC1.pin10, IC1.pin13
  N3: T-Cobbler1.#22, S1.SW, R1.Pin_1
  N4: T-Cobbler1.5.0V#20, IC1.pin1, IC1.pin9, IC1.pin14, S1.VCC, R1.Pin_0
  N5: T-Cobbler1.GND#22, IC1.pin7, IC1.pin8, S1.GND
  N6: T-Cobbler1.#18, IC1.pin12
  N7: IC1.pin3, S1.VRX
  N8: IC1.pin4, S1.VRY

custom parts:
  GPIO Extension Board: T-Cobbler for RPi B+ and Rpi2 from SunFounder
  Joystick PS2 v1.0: A joystick is an input device consisting of a stick that pivots on a base and reports its angle or direction to the device it is controlling. Joysticks are often used to control video games and robots. A Joystick PS2 is used here.
