# Fritzing sketch 2.2.1_Photoresistor (saved by Fritzing 0.9.3b)
breadboards: 1

parts:
  T-Cobbler1 = GPIO Extension Board
  IC1 = IC, DIP package, 14 pins [chip_label=ADC0834]
  R2 = Resistor [tolerance=±5% resistance=220 package=THT]
  LED1 = LED - 5mm [color="Red (633nm)" package="5 mm [THT]"]
  C1 = Photoresistor [package=cap-pth-small2]
  R3 = Resistor [tolerance=±5% resistance=10k package=THT]

nets:
  N1: T-Cobbler1.#17, IC1.pin2
  N2: T-Cobbler1.#27, IC1.pin10, IC1.pin13
  N3: T-Cobbler1.#22, R2.Pin_1
  N4: T-Cobbler1.5.0V#20, IC1.pin1, IC1.pin9, IC1.pin14, R3.Pin_1
  N5: T-Cobbler1.GND#22, IC1.pin7, IC1.pin8, LED1.cathode, C1.1
  N6: T-Cobbler1.#18, IC1.pin12
  N7: IC1.pin3, C1.2, R3.Pin_0
  N8: R2.Pin_0, LED1.anode

custom parts:
  GPIO Extension Board: T-Cobbler for RPi B+ and Rpi2 from SunFounder
