# Fritzing sketch 2.2.2_Thermistor (saved by Fritzing 0.9.3b)
breadboards: 1

parts:
  T-Cobbler1 = GPIO Extension Board
  IC1 = IC, DIP package, 14 pins [chip_label=ADC0834]
  R3 = Resistor [tolerance=±5% resistance=10k package=THT]
  R4 = Temperature Sensor (Thermistor) [thermistor_type=NTC package=THT]

nets:
  N1: T-Cobbler1.#17, IC1.pin2
  N2: T-Cobbler1.#27, IC1.pin10, IC1.pin13
  N3: T-Cobbler1.5.0V#20, IC1.pin1, IC1.pin9, IC1.pin14, R3.Pin_1
  N4: T-Cobbler1.GND#22, IC1.pin7, IC1.pin8, R4.pin_0
  N5: T-Cobbler1.#18, IC1.pin12
  N6: IC1.pin3, R3.Pin_0, R4.pin_1

custom parts:
  GPIO Extension Board: T-Cobbler for RPi B+ and Rpi2 from SunFounder
