# Fritzing sketch 2.2.3_DHT (saved by Fritzing 0.9.3b)
breadboards: 1

parts:
  T-Cobbler1 = T-Cobbler
  R1 = Resistor [tolerance=±5% resistance=10k package=THT]
  S2 = Humiture Sensor v1.0 [package=THT]

nets:
  N1: T-Cobbler1.#17, R1.Pin_0, S2.+
  N2: T-Cobbler1.3.3V, R1.Pin_1, S2.out
  N3: T-Cobbler1.GND#12, S2.-

custom parts:
  T-Cobbler: T-Cobbler for RPi B+ and Rpi2 from SunFounder
  Humiture Sensor v1.0: Humiture Sensor www.sunfounder.com
