# Fritzing sketch 2.2.4_PIR (saved by Fritzing 0.9.3b)
breadboards: 1

parts:
  T-Cobbler1 = GPIO Extension Board
  S1 = PIR2 [package=THT]
  R1 = Resistor [tolerance=±5% resistance=220 package=THT]
  LED1 = RGB LED (com. cathode, rgb) [package="5 mm [THT]"]
  R2 = Resistor [tolerance=±5% resistance=220 package=THT]
  R3 = Resistor [tolerance=±5% resistance=220 package=THT]

nets:
  3V3: T-Cobbler1.3V3, S1.VCC
  N1: T-Cobbler1.GND#4, S1.GND
  N2: T-Cobbler1.#17, S1.OUT
  N3: T-Cobbler1.#27, R2.Pin_1
  N4: T-Cobbler1.#22, R3.Pin_1
  N5: T-Cobbler1.#18, R1.Pin_1
  N6: T-Cobbler1.GND#26, LED1.common_cathode
  N7: R1.Pin_0, LED1.red_anode
  N8: LED1.green_anode, R2.Pin_0
  N9: LED1.blue_anode, R3.Pin_0

custom parts:
  GPIO Extension Board: T-Cobbler for RPi B+ and Rpi2 from SunFounder
