# Fritzing sketch 2.2.5_Ultrasonic (saved by Fritzing 0.9.3b)
breadboards: 1

parts:
  T-Cobbler1 = T-Cobbler
  HC-SR04_Sensor_1 = HC-SR04 Ultrasonic Distance Sensor

nets:
  N1: T-Cobbler1.5.0V#20, HC-SR04_Sensor_1.VCC
  N2: T-Cobbler1.#23, HC-SR04_Sensor_1.TRIG
  N3: T-Cobbler1.#24, HC-SR04_Sensor_1.ECHO
  N4: T-Cobbler1.GND#29, HC-SR04_Sensor_1.GND

custom parts:
  T-Cobbler: T-Cobbler for RPi B+ and Rpi2 from SunFounder
