# Fritzing sketch 2.2.7_RFID (saved by Fritzing 0.9.3b)
breadboards: 1

parts:
  T-Cobbler1 = T-Cobbler
  module1 = RFID-RC522-blue

nets:
  3.3V: T-Cobbler1.3.3V, module1.3.3V
  N1: T-Cobbler1.MOSI, module1.MOSI
  N2: T-Cobbler1.MISO, module1.MISO
  N3: T-Cobbler1.SCLK, module1.SCK
  N4: T-Cobbler1.GND#12, module1.GND
  N5: T-Cobbler1.#25, module1.RST
  N6: T-Cobbler1.CE0, module1.SDA

custom parts:
  T-Cobbler: T-Cobbler for RPi B+ and Rpi2 from SunFounder
  RFID-RC522-blue: RFID-RC522 module from Sunfounder
