# Fritzing sketch 2.2.8_VibrationTilt (saved by Fritzing 0.9.3b)
breadboards: 1

parts:
  T-Cobbler1 = T-Cobbler
  S1 = Tilt Switch [package=THT]
  LED1 = LED - 5mm [color="Red (633nm)" package="5 mm [THT]"]
  LED2 = LED - 5mm [color="Green (555nm)" package="5 mm [THT]"]
  R1 = Resistor [tolerance=±5% resistance=10k package=THT]
  R2 = Resistor [tolerance=±5% resistance=220 package=THT]
  R3 = Resistor [tolerance=±5% resistance=220 package=THT]

nets:
  N1: T-Cobbler1.#17, S1.Pin_1, R1.Pin_0
  N2: T-Cobbler1.#27, LED2.anode
  N3: T-Cobbler1.#22, LED1.anode
  N4: T-Cobbler1.3.3V, R1.Pin_1
  N5: T-Cobbler1.GND#12, S1.Pin_2, R2.Pin_1, R3.Pin_1
  N6: LED1.cathode, R3.Pin_0
  N7: LED2.cathode, R2.Pin_0

custom parts:
  T-Cobbler: T-Cobbler for RPi B+ and Rpi2 from SunFounder
