# Fritzing sketch 3.1.10 Alarm Bell (saved by Fritzing 0.9.3b)
breadboards: 1

parts:
  T-Cobbler1 = GPIO Extension Board
  LED1 = LED - 5mm [color="Green (560nm)" package="5 mm [THT]"]
  R2 = Resistor [tolerance=±5% resistance=220 package=THT]
  Q1 = NPN-Transistor [package="TO92 [THT]"]
  R3 = Resistor [tolerance=±5% resistance=1k package=THT]
  S1 = buzzer [package="[THT]"]
  LED2 = LED - 5mm [color="Red (633nm)" package="5 mm [THT]"]
  R4 = Resistor [tolerance=±5% resistance=220 package=THT]
  S2 = Toggle Switch [package=THT]
  R5 = Resistor [tolerance=±5% resistance=10k package=THT]
  104 = Ceramic Capacitor [capacitance=100nF package="100 mil [THT, multilayer]"]

nets:
  3V3: T-Cobbler1.3V3, S1.VCC, S2.L2
  N1: T-Cobbler1.GND#4, LED1.cathode, Q1.E, LED2.cathode, S2.L1, R5.Pin_0, 104.0
  N2: T-Cobbler1.#17, R2.Pin_1
  N3: T-Cobbler1.#27, R4.Pin_1
  N4: T-Cobbler1.#22, R3.Pin_1
  N5: T-Cobbler1.#18, S2.COM, R5.Pin_1, 104.1
  N6: LED1.anode, R2.Pin_0
  N7: Q1.B, R3.Pin_0
  N8: LED2.anode, R4.Pin_0

custom parts:
  GPIO Extension Board: T-Cobbler for RPi B+ and Rpi2 from SunFounder
