# Fritzing sketch 3.1.11 Morse Code Generator (saved by Fritzing 0.9.3b)
breadboards: 1

parts:
  T-Cobbler1 = GPIO Extension Board
  LED1 = LED - 5mm [color="Red (633nm)" package="5 mm [THT]"]
  R2 = Resistor [tolerance=±5% resistance=220 package=THT]
  Q1 = NPN-Transistor [package="TO92 [THT]"]
  R3 = Resistor [tolerance=±5% resistance=1k package=THT]
  S1 = buzzer [package="[THT]"]

nets:
  3V3: T-Cobbler1.3V3, S1.VCC
  N1: T-Cobbler1.GND#4, LED1.cathode, Q1.E
  N2: T-Cobbler1.#17, R2.Pin_1
  N3: T-Cobbler1.#22, R3.Pin_1
  N4: LED1.anode, R2.Pin_0
  N5: Q1.B, R3.Pin_0
  N6: Q1.C, S1.GND

custom parts:
  GPIO Extension Board: T-Cobbler for RPi B+ and Rpi2 from SunFounder
