# Fritzing sketch 3.1.12 GAME - Guess Number (saved by Fritzing 0.9.3b)
breadboards: 1

parts:
  T-Cobbler1 = GPIO Extension Board
  IC2 = 4*4 keyboard [chip_label=IC package="DIP (Dual Inline) [THT]"]
  R1 = Resistor [tolerance=±5% resistance=10k package=THT]
  R2 = Resistor [tolerance=±5% resistance=10k package=THT]
  R3 = Resistor [tolerance=±5% resistance=10k package=THT]
  R4 = Resistor [tolerance=±5% resistance=10k package=THT]
  R5 = Resistor [tolerance=±5% resistance=10k package=THT]
  R6 = Resistor [tolerance=±5% resistance=10k package=THT]
  R7 = Resistor [tolerance=±5% resistance=10k package=THT]
  R8 = Resistor [tolerance=±5% resistance=10k package=THT]
  module1 = I2C LCD1602

nets:
  N1: T-Cobbler1.SDA1, module1.SDA
  N2: T-Cobbler1.SCL1, module1.SCL
  N3: T-Cobbler1.GND#4, R1.Pin_1, R2.Pin_1, R3.Pin_1, R4.Pin_1, R5.Pin_1, R6.Pin_1, R7.Pin_1, R8.Pin_1
  N4: T-Cobbler1.#17, IC2.Y4, R8.Pin_0
  N5: T-Cobbler1.#27, IC2.Y3, R7.Pin_0
  N6: T-Cobbler1.#22, IC2.Y2, R6.Pin_0
  N7: T-Cobbler1.MOSI, IC2.Y1, R5.Pin_0
  N8: T-Cobbler1.5.0V#20, module1.VCC
  N9: T-Cobbler1.GND#22, module1.GND
  N10: T-Cobbler1.#18, IC2.X1, R1.Pin_0
  N11: T-Cobbler1.#23, IC2.X2, R2.Pin_0
  N12: T-Cobbler1.#24, IC2.X3, R3.Pin_0
  N13: T-Cobbler1.#25, IC2.X4, R4.Pin_0

custom parts:
  GPIO Extension Board: T-Cobbler for RPi B+ and Rpi2 from SunFounder
  4*4 keyboard: A 4*4 keyboard
  I2C LCD1602: I2C LCD1602 module of SunFounder Sensor Kit
