# Fritzing sketch 3.1.14 GAME - Not Not (saved by Fritzing 0.9.3b)
breadboards: 1

parts:
  T-Cobbler1 = GPIO Extension Board
  U1 = 74HC595 [package="DIP16 [THT]"]
  U2 = 74HC595 [package="DIP16 [THT]"]
  module2 = 788BS Dot matix
  S1 = Pushbutton [package="[THT]"]
  S2 = Pushbutton [package="[THT]"]
  R1 = Resistor [tolerance=±5% resistance=10k package=THT]
  R2 = Resistor [tolerance=±5% resistance=10k package=THT]

nets:
  VCC: T-Cobbler1.3V3, U1.MR, U1.VCC, U2.MR, U2.VCC, S1.Pin_1, S1.Pin_2, S2.Pin_1, S2.Pin_2
  GND: T-Cobbler1.GND#4, U1.GND, U2.GND, R1.Pin_1, R2.Pin_1
  N1: T-Cobbler1.#17, U2.DS
  N2: T-Cobbler1.#27, U1.SH_CP, U2.SH_CP
  N3: T-Cobbler1.#26, S1.Pin_3, S1.Pin_4, R1.Pin_0
  N4: T-Cobbler1.GND#22, U1.OE, U2.OE
  N5: T-Cobbler1.#18, U1.ST_CP, U2.ST_CP
  N6: T-Cobbler1.#20, S2.Pin_3, S2.Pin_4, R2.Pin_0
  N7: U1.Q1, module2.P6
  N8: U1.Q2, module2.P5
  N9: U1.Q3, module2.P10
  N10: U1.Q4, module2.P3
  N11: U1.Q5, module2.P11
  N12: U1.Q6, module2.P15
  N13: U1.Q7, module2.P16
  N14: U1.DS, U2.Q7'
  N15: U1.Q0, module2.P13
  N16: U2.Q1, module2.P14
  N17: U2.Q2, module2.P1
  N18: U2.Q3, module2.P12
  N19: U2.Q4, module2.P8
  N20: U2.Q5, module2.P2
  N21: U2.Q6, module2.P7
  N22: U2.Q7, module2.P4
  N23: U2.Q0, module2.P9

custom parts:
  GPIO Extension Board: T-Cobbler for RPi B+ and Rpi2 from SunFounder
  788BS Dot matix: 788BS 8x8 dot matix from SunFounder
  Pushbutton: A generic pushbutton.
