# Fritzing sketch 3.1.1_ReversingAlarm (saved by Fritzing 0.9.3b)
breadboards: 1

parts:
  T-Cobbler1 = T-Cobbler
  S1 = buzzer [package="[THT]"]
  R1 = Resistor [tolerance=±10% resistance=1k package=THT]
  Q1 = NPN-Transistor [package="TO92 [THT]"]
  module1 = I2C LCD1602
  U1 = HC-SR04 [chip_label=IC package="SIP (Single Inline) [THT]"]

nets:
  N1: T-Cobbler1.SDA, module1.SDA
  N2: T-Cobbler1.SCL, module1.SCL
  N3: T-Cobbler1.GND#4, Q1.E, module1.GND
  N4: T-Cobbler1.#17, R1.Pin_1
  3.3V: T-Cobbler1.3.3V, S1.VCC
  VCC: T-Cobbler1.5.0V#20, module1.VCC, U1.Vcc
  N5: T-Cobbler1.#23, U1.Trig
  N6: T-Cobbler1.#24, U1.Echo
  N7: T-Cobbler1.GND#29, U1.GND
  N8: S1.GND, Q1.C
  N9: R1.Pin_0, Q1.B

custom parts:
  T-Cobbler: T-Cobbler for RPi B+ and Rpi2 from SunFounder
  I2C LCD1602: I2C LCD1602 module of SunFounder Sensor Kit
  HC-SR04: HC-SR04 ultrasound distance sensor
