# Fritzing sketch 3.1.2_TrafficLight (saved by Fritzing 0.9.3b)
breadboards: 1

parts:
  T-Cobbler1 = T-Cobbler
  R1 = Resistor [tolerance=±5% resistance=1k package=THT]
  U1 = 74HC595 [package="DIP16 [THT]"]
  Q1 = PNP-Transistor [package="TO92 [THT]"]
  Q2 = PNP-Transistor [package="TO92 [THT]"]
  Q3 = PNP-Transistor [package="TO92 [THT]"]
  Q4 = PNP-Transistor [package="TO92 [THT]"]
  LED1 = 7-SEGMENT-4DIGIT-YOUNGSUN [package=7-segment-4digit-youngsun-longpads]
  R3 = Resistor [tolerance=±5% resistance=1k package=THT]
  R4 = Resistor [tolerance=±5% resistance=1k package=THT]
  R5 = Resistor [tolerance=±5% resistance=1k package=THT]
  R6 = Resistor [tolerance=±5% resistance=220 package=THT]
  R7 = Resistor [tolerance=±5% resistance=220 package=THT]
  R8 = Resistor [tolerance=±5% resistance=220 package=THT]
  R9 = Resistor [tolerance=±5% resistance=220 package=THT]
  R10 = Resistor [tolerance=±5% resistance=220 package=THT]
  R11 = Resistor [tolerance=±5% resistance=220 package=THT]
  R12 = Resistor [tolerance=±5% resistance=220 package=THT]
  R13 = Resistor [tolerance=±5% resistance=220 package=THT]
  LED2 = LED - 5mm [color="Green (565nm)" package="5 mm [THT]"]
  LED3 = LED - 5mm [color="Yellow (595nm)" package="5 mm [THT]"]
  LED4 = LED - 5mm [color="Red (633nm)" package="5 mm [THT]"]
  R14 = Resistor [tolerance=±5% resistance=220 package=THT]
  R15 = Resistor [tolerance=±5% resistance=220 package=THT]
  R16 = Resistor [tolerance=±5% resistance=220 package=THT]

nets:
  3V3: T-Cobbler1.3V3, U1.MR, U1.VCC, Q1.E, Q2.E, Q3.E, Q4.E, R14.Pin_1, R15.Pin_1, R16.Pin_1
  N1: T-Cobbler1.GND#4, U1.GND
  N2: T-Cobbler1.#17, R5.Pin_0
  N3: T-Cobbler1.#27, R4.Pin_0
  N4: T-Cobbler1.#22, R3.Pin_0
  N5: T-Cobbler1.MOSI, R1.Pin_0
  N6: T-Cobbler1.GND#22, U1.OE
  N7: T-Cobbler1.#18, U1.SH_CP
  N8: T-Cobbler1.#23, U1.ST_CP
  N9: T-Cobbler1.#24, U1.DS
  N10: T-Cobbler1.#25, LED4.cathode
  N11: T-Cobbler1.CE0, LED2.cathode
  N12: T-Cobbler1.CE1, LED3.cathode
  N13: R1.Pin_1, Q1.B
  N14: U1.Q1, R7.Pin_1
  N15: U1.Q2, R8.Pin_1
  N16: U1.Q3, R9.Pin_0
  N17: U1.Q4, R10.Pin_0
  N18: U1.Q5, R11.Pin_0
  N19: U1.Q6, R12.Pin_1
  N20: U1.Q7, R13.Pin_0
  N21: U1.Q0, R6.Pin_0
  N22: Q1.C, LED1.DP
  N23: Q2.B, R3.Pin_1
  N24: Q2.C, LED1.F
  N25: Q3.B, R4.Pin_1
  N26: Q3.C, LED1.COL-C
  N27: Q4.B, R5.Pin_1
  N28: Q4.C, LED1.G
  N29: LED1.DIG2, R10.Pin_1
  N30: LED1.D, R9.Pin_1
  N31: LED1.COL-A, R13.Pin_1
  N32: LED1.E, R8.Pin_0
  N33: LED1.DIG3, R12.Pin_0
  N34: LED1.APOS-A, R7.Pin_0
  N35: LED1.C, R11.Pin_1
  N36: LED1.A, R6.Pin_1
  N37: LED2.anode, R14.Pin_0
  N38: LED3.anode, R15.Pin_0
  N39: LED4.anode, R16.Pin_0

custom parts:
  T-Cobbler: T-Cobbler for RPi B+ and Rpi2 from SunFounder
  7-SEGMENT-4DIGIT-YOUNGSUN: This is a part for the 4-Digit 7-segment LEDs from Young Sun. Different from the Digikey LEDs, all 16 pins are used. The LONGPADS Variant is used for a test jig, but you may like it because there is more pad to solder to. If you are concerned about routing space, the standard works just fine though.
