# Fritzing sketch 3.1.4 Smart Fan (saved by Fritzing 0.9.3b)
breadboards: 1

parts:
  T-Cobbler1 = GPIO Extension Board
  IC1 = IC, DIP package, 14 pins [chip_label=ADC0834]
  R3 = Resistor [tolerance=±5% resistance=10k package=THT]
  R4 = Temperature Sensor (Thermistor) [thermistor_type=NTC package=THT]
  IC2 = Power Module V1.0 [package=THT]
  M1 = DC Motor
  IC3 = IC, DIP package, 16 pins [chip_label=L293D]
  S1 = Pushbutton [package="[THT]"]
  R5 = Resistor [tolerance=±5% resistance=10k package=THT]

nets:
  N1: T-Cobbler1.GND#4, IC1.pin7, IC2.-#4, IC3.pin5
  N2: T-Cobbler1.#17, IC1.pin2
  N3: T-Cobbler1.#27, IC1.pin10, IC1.pin13
  N4: T-Cobbler1.#22, S1.Pin_3, S1.Pin_4, R5.Pin_0
  N5: T-Cobbler1.#5, IC3.pin2
  N6: T-Cobbler1.#6, IC3.pin7
  N7: T-Cobbler1.#13, IC3.pin1
  N8: T-Cobbler1.5.0V#20, IC1.pin1, IC1.pin9, IC1.pin14, R3.Pin_1
  N9: T-Cobbler1.#18, IC1.pin12
  N10: IC1.pin3, R3.Pin_0, R4.pin_1
  N11: IC1.pin8, R4.pin_0, IC2.-#5, S1.Pin_1, S1.Pin_2
  N12: IC2.+#2, IC3.pin8, R5.Pin_1
  N13: IC2.+#3, IC3.pin16
  N14: M1.pin_1, IC3.pin6
  N15: M1.pin_2, IC3.pin3

custom parts:
  GPIO Extension Board: T-Cobbler for RPi B+ and Rpi2 from SunFounder
  Power Module V1.0: Power Module used for BreadBoard www.sunfounder.com
  Pushbutton: A generic pushbutton.
