# Fritzing sketch 3.1.4_Welcome (saved by Fritzing 0.9.3b)
breadboards: 1

parts:
  T-Cobbler1 = GPIO Extension Board
  S1 = PIR2 [package=THT]
  LED1 = LED - 5mm [color="Red (633nm)" package="5 mm [THT]"]
  R1 = Resistor [tolerance=±5% resistance=220 package=THT]
  S2 = buzzer [package="[THT]"]
  Q1 = PNP-Transistor [package="TO92 [THT]"]
  R2 = Resistor [tolerance=±5% resistance=1k package=THT]
  module1 = Servo

nets:
  VCC: T-Cobbler1.3V3, S1.VCC, S2.VCC
  N1: T-Cobbler1.GND#4, S1.GND, R1.Pin_1, Q1.C
  N2: T-Cobbler1.#17, S1.OUT
  N3: T-Cobbler1.#27, R2.Pin_1
  N4: T-Cobbler1.#22, module1.Orange
  N5: T-Cobbler1.5.0V#20, module1.Red
  N6: T-Cobbler1.#18, LED1.anode
  N7: T-Cobbler1.GND#26, module1.Brown
  N8: LED1.cathode, R1.Pin_0
  N9: S2.GND, Q1.E
  N10: Q1.B, R2.Pin_0

custom parts:
  GPIO Extension Board: T-Cobbler for RPi B+ and Rpi2 from SunFounder
  Servo: servo
