# Fritzing sketch 3.1.5 Battery Indicator (saved by Fritzing 0.9.3b)
breadboards: 1

parts:
  IC1 = IC, DIP package, 14 pins [chip_label=ADC0834]
  R2 = Resistor [tolerance=±5% resistance=10k package=THT]
  D1 = LED_BARGRAPH_10 [package=led_bargaph_10]
  R3 = Resistor [tolerance=±5% resistance=10k package=THT]
  R4 = Resistor [tolerance=±5% resistance=10k package=THT]
  R5 = Resistor [tolerance=±5% resistance=10k package=THT]
  R6 = Resistor [tolerance=±5% resistance=10k package=THT]
  R7 = Resistor [tolerance=±5% resistance=10k package=THT]
  R8 = Resistor [tolerance=±5% resistance=10k package=THT]
  R9 = Resistor [tolerance=±5% resistance=10k package=THT]
  R10 = Resistor [tolerance=±5% resistance=10k package=THT]
  R11 = Resistor [tolerance=±5% resistance=10k package=THT]
  R12 = Resistor [tolerance=±5% resistance=10k package=THT]
  T-Cobbler2 = GPIO Extension Board

nets:
  N1: IC1.pin1, IC1.pin9, IC1.pin14, T-Cobbler2.5.0V#20
  N2: IC1.pin2, T-Cobbler2.#17
  N3: IC1.pin3, R2.Pin_0
  N4: IC1.pin7, R2.Pin_1, T-Cobbler2.GND#4
  N5: IC1.pin8, T-Cobbler2.GND#22
  N6: IC1.pin10, IC1.pin13, T-Cobbler2.#27
  N7: IC1.pin12, T-Cobbler2.#18
  N8: D1.A_A, R3.Pin_1
  N9: D1.B_A, R4.Pin_1
  N10: D1.C_A, R5.Pin_0
  N11: D1.D_A, R6.Pin_0
  N12: D1.E_A, R7.Pin_0
  N13: D1.F_A, R8.Pin_0
  N14: D1.G_A, R9.Pin_0
  N15: D1.H_A, R11.Pin_0
  N16: D1.I_A, R12.Pin_0
  N17: D1.J_A, R10.Pin_0
  N18: D1.J_C, T-Cobbler2.#26
  N19: D1.I_C, T-Cobbler2.#19
  N20: D1.H_C, T-Cobbler2.#13
  N21: D1.G_C, T-Cobbler2.#6
  N22: D1.F_C, T-Cobbler2.#5
  N23: D1.E_C, T-Cobbler2.#21
  N24: D1.D_C, T-Cobbler2.#20
  N25: D1.C_C, T-Cobbler2.#16
  N26: D1.B_C, T-Cobbler2.#12
  N27: D1.A_C, T-Cobbler2.#25
  N28: R3.Pin_0, R4.Pin_0, R5.Pin_1, R6.Pin_1, R7.Pin_1, R8.Pin_1, R9.Pin_1, R10.Pin_1, R11.Pin_1, R12.Pin_1, T-Cobbler2.3V3

notes:
  The Measured Object

custom parts:
  GPIO Extension Board: T-Cobbler for RPi B+ and Rpi2 from SunFounder
