# Fritzing sketch 3.1.6 Motion Control (saved by Fritzing 0.9.3b)
breadboards: 1

parts:
  T-Cobbler1 = GPIO Extension Board
  IC2 = Power Module V1.0 [package=THT]
  U1 = Stepper Motor Driver-v1.0 [package="DIP28 [THT]"]
  module1 = Step Motor
  Part1 = InvenSense MPU6050

nets:
  3V3: T-Cobbler1.3V3, Part1.VCC
  N1: T-Cobbler1.SDA1, Part1.SDA
  N2: T-Cobbler1.SCL1, Part1.SCL
  N3: T-Cobbler1.GND#4, Part1.GND
  N4: T-Cobbler1.GND#22, IC2.-#5, U1.-
  N5: T-Cobbler1.#18, U1.IN1
  N6: T-Cobbler1.#23, U1.IN2
  N7: T-Cobbler1.#24, U1.IN3
  N8: T-Cobbler1.#25, U1.IN4
  N9: IC2.3.3V, IC2.-#4
  N10: IC2.+#2, IC2.GND
  N11: IC2.+#3, U1.+
  N12: U1.OUT1, module1.blue
  N13: U1.OUT2, module1.pink
  N14: U1.OUT3, module1.yellow
  N15: U1.OUT4, module1.orange
  N16: U1.COM, module1.red

custom parts:
  GPIO Extension Board: T-Cobbler for RPi B+ and Rpi2 from SunFounder
  Power Module V1.0: Power Module used for BreadBoard www.sunfounder.com
  Stepper Motor Driver-v1.0: Stepper Motor Driver
  Step Motor: step motor
