# Fritzing sketch 3.1.7_TrafficLight (saved by Fritzing 0.9.3b)
breadboards: 1

parts:
  T-Cobbler1 = GPIO Extension Board
  U1 = 74HC595 [package="DIP16 [THT]"]
  LED1 = 7-SEGMENT-4DIGIT-YOUNGSUN [package=7-segment-4digit-youngsun-longpads]
  R8 = Resistor [tolerance=±5% resistance=220 package=THT]
  R9 = Resistor [tolerance=±5% resistance=220 package=THT]
  R10 = Resistor [tolerance=±5% resistance=220 package=THT]
  R12 = Resistor [tolerance=±5% resistance=220 package=THT]
  LED2 = LED - 5mm [color="Red (633nm)" package="5 mm [THT]"]
  LED3 = LED - 5mm [color="Green (560nm)" package="5 mm [THT]"]
  LED4 = LED - 5mm [color="Yellow (595nm)" package="5 mm [THT]"]
  R13 = Resistor [tolerance=±5% resistance=220 package=THT]
  R14 = Resistor [tolerance=±5% resistance=220 package=THT]
  R15 = Resistor [tolerance=±5% resistance=220 package=THT]

nets:
  3V3: T-Cobbler1.3V3, U1.MR, U1.VCC, R13.Pin_1, R14.Pin_1, R15.Pin_1
  N1: T-Cobbler1.GND#4, U1.GND
  N2: T-Cobbler1.#17, R8.Pin_1
  N3: T-Cobbler1.#27, R12.Pin_1
  N4: T-Cobbler1.#22, R9.Pin_1
  N5: T-Cobbler1.MOSI, R10.Pin_1
  N6: T-Cobbler1.GND#22, U1.OE
  N7: T-Cobbler1.#18, U1.SH_CP
  N8: T-Cobbler1.#23, U1.ST_CP
  N9: T-Cobbler1.#24, U1.DS
  N10: T-Cobbler1.#25, LED2.cathode
  N11: T-Cobbler1.CE0, LED3.cathode
  N12: T-Cobbler1.CE1, LED4.cathode
  N13: U1.Q1, LED1.APOS-A
  N14: U1.Q2, LED1.E
  N15: U1.Q3, LED1.D
  N16: U1.Q4, LED1.DIG2
  N17: U1.Q5, LED1.C
  N18: U1.Q6, LED1.DIG3
  N19: U1.Q7, LED1.COL-A
  N20: U1.Q0, LED1.A
  N21: LED1.DP, R10.Pin_0
  N22: LED1.F, R9.Pin_0
  N23: LED1.COL-C, R12.Pin_0
  N24: LED1.G, R8.Pin_0
  N25: LED2.anode, R13.Pin_0
  N26: LED3.anode, R14.Pin_0
  N27: LED4.anode, R15.Pin_0

custom parts:
  GPIO Extension Board: T-Cobbler for RPi B+ and Rpi2 from SunFounder
  7-SEGMENT-4DIGIT-YOUNGSUN: This is a part for the 4-Digit 7-segment LEDs from Young Sun. Different from the Digikey LEDs, all 16 pins are used. The LONGPADS Variant is used for a test jig, but you may like it because there is more pad to solder to. If you are concerned about routing space, the standard works just fine though.
