# Fritzing sketch 3.1.8 Overheat Monitor (saved by Fritzing 0.9.3b)
breadboards: 1

parts:
  T-Cobbler1 = GPIO Extension Board
  IC1 = IC, DIP package, 14 pins [chip_label=ADC0834]
  S1 = Joystick PS2 v1.0 [package=THT]
  R1 = Resistor [tolerance=±5% resistance=10k package=THT]
  LED1 = LED - 5mm [color="Red (633nm)" package="5 mm [THT]"]
  R3 = Resistor [tolerance=±5% resistance=220 package=THT]
  R5 = Resistor [tolerance=±5% resistance=10k package=THT]
  S2 = buzzer [package="[THT]"]
  Q1 = NPN-Transistor [package="TO92 [THT]"]
  R6 = Resistor [tolerance=±5% resistance=1k package=THT]
  R7 = Temperature Sensor (Thermistor) [thermistor_type=NTC package=THT]
  module1 = I2C LCD1602

nets:
  3V3: T-Cobbler1.3V3, R1.Pin_0, S2.VCC
  N1: T-Cobbler1.SDA1, module1.SDA
  N2: T-Cobbler1.SCL1, module1.SCL
  N3: T-Cobbler1.GND#4, IC1.pin7, S1.GND, LED1.cathode, Q1.E, R7.pin_1
  N4: T-Cobbler1.#17, IC1.pin2
  N5: T-Cobbler1.#27, IC1.pin10, IC1.pin13
  N6: T-Cobbler1.#22, S1.SW, R1.Pin_1
  VCC: T-Cobbler1.5.0V#20, IC1.pin1, IC1.pin9, IC1.pin14, S1.VCC, R5.Pin_0, module1.VCC
  N7: T-Cobbler1.GND#22, IC1.pin8, module1.GND
  N8: T-Cobbler1.#18, IC1.pin12
  N9: T-Cobbler1.#23, R6.Pin_1
  N10: T-Cobbler1.#24, R3.Pin_1
  N11: IC1.pin3, R5.Pin_1, R7.pin_0
  N12: IC1.pin4, S1.VRX
  N13: IC1.pin5, S1.VRY
  N14: LED1.anode, R3.Pin_0
  N15: S2.GND, Q1.C
  N16: Q1.B, R6.Pin_0

custom parts:
  GPIO Extension Board: T-Cobbler for RPi B+ and Rpi2 from SunFounder
  Joystick PS2 v1.0: A joystick is an input device consisting of a stick that pivots on a base and reports its angle or direction to the device it is controlling. Joysticks are often used to control video games and robots. A Joystick PS2 is used here.
  I2C LCD1602: I2C LCD1602 module of SunFounder Sensor Kit
